# Fritzing sketch raspiledchaser (saved by Fritzing 0.7.7b)
breadboards: 1

parts:
  R2 = Resistor [tolerance=±5% resistance=330 package=THT]
  R6 = Resistor [tolerance=±5% resistance=330 package=THT]
  R4 = Resistor [tolerance=±5% resistance=330 package=THT]
  R8 = Resistor [tolerance=±5% resistance=330 package=THT]
  R1 = Resistor [tolerance=±5% resistance=330 package=THT]
  R7 = Resistor [tolerance=±5% resistance=330 package=THT]
  R3 = Resistor [tolerance=±5% resistance=330 package=THT]
  R5 = Resistor [tolerance=±5% resistance=330 package=THT]
  LED3 = LED - 5mm [color="Green (555nm)" package="5 mm [THT]"]
  LED1 = LED - 5mm [color="Green (555nm)" package="5 mm [THT]"]
  LED4 = LED - 5mm [color="Green (555nm)" package="5 mm [THT]"]
  LED7 = LED - 5mm [color="Yellow (585nm)" package="5 mm [THT]"]
  LED2 = LED - 5mm [color="Green (555nm)" package="5 mm [THT]"]
  LED6 = LED - 5mm [color="Yellow (585nm)" package="5 mm [THT]"]
  LED5 = LED - 5mm [color="Green (555nm)" package="5 mm [THT]"]
  RaspberryPi1 = Raspberry Pi Model B
  LED8 = LED - 5mm [color="Red (633nm)" package="5 mm [THT]"]

nets:
  N1: R2.Pin_0, RaspberryPi1.#17
  N2: R2.Pin_1, LED2.anode
  N3: R6.Pin_0, RaspberryPi1.#23
  N4: R6.Pin_1, LED6.anode
  N5: R4.Pin_0, RaspberryPi1.#21
  N6: R4.Pin_1, LED4.anode
  N7: R8.Pin_0, RaspberryPi1.#25
  N8: R8.Pin_1, LED8.anode
  N9: R1.Pin_0, RaspberryPi1.#4
  N10: R1.Pin_1, LED1.anode
  N11: R7.Pin_0, RaspberryPi1.#24
  N12: R7.Pin_1, LED7.anode
  N13: R3.Pin_0, RaspberryPi1.#18
  N14: R3.Pin_1, LED3.anode
  N15: R5.Pin_0, RaspberryPi1.#22
  N16: R5.Pin_1, LED5.anode
  N17: LED3.cathode, LED1.cathode, LED4.cathode, LED7.cathode, LED2.cathode, LED6.cathode, LED5.cathode, RaspberryPi1.GND, LED8.cathode

custom parts:
  Raspberry Pi Model B: Raspberry Pi (Model B)
